# Fritzing sketch arduino voiture (saved by Fritzing 0.9.3b)

parts:
  Composant1 = Arduino Motor Shield (Rev3)
  Composant2 = Bluetooth HC-05 Macho
  J1 = Piezo Speaker
  R2 = Resistor [tolerance=±5% resistance=2.2k package="0603 [SMD]"]
  hc-sr2 = hc-sr04
  M1 = DC Motor
  LED1 = smd LED [color="Red (633nm)" package="0603 [SMD]"]
  R4 = Resistor [tolerance=±5% resistance=220 package="0603 [SMD]"]
  R5 = Resistor [tolerance=±5% resistance=10k package="0603 [SMD]"]
  R1 = Resistor [tolerance=±5% resistance=1k package="0603 [SMD]"]
  LED2 = smd LED [color="Red (633nm)" package="0603 [SMD]"]
  J2 = Basic Servo
  R6 = PHOTOCELL [package=photocell]

nets (from the schematic view):
  GND: Composant1.GND, Composant2.GND, J1.pin1, R2.Pin_0, hc-sr2.GND, R4.Pin_1, R5.Pin_1, J2.gnd
  N1: Composant1.A0, R5.Pin_0, R6.P$1
  N2: Composant1.D8/BreakeB, R1.Pin_1
  N3: Composant1.D10_PWM, LED1.anode, LED2.anode
  N4: Composant1.D3_PWM/A, J1.pin2
  N5: Composant1.D4, hc-sr2.Echo
  N6: Composant1.D5_PWM, hc-sr2.Trig
  N7: Composant1.D7, Composant2.RXD
  N8: Composant1.A-, M1.pin_2
  N9: Composant1.A+, M1.pin_1
  GND_2: Composant1.VMOT
  N10: Composant1.D6_PWM, J2.pulse
  VCC: Composant1.5V, Composant2.VCC, hc-sr2.VCC, J2.vcc, R6.P$2
  5V: Composant1.VIN
  N11: Composant2.TXD, R2.Pin_1, R1.Pin_0
  N12: LED1.cathode, R4.Pin_0, LED2.cathode

custom parts:
  hc-sr04: This is a HC-SR04 Distance Sensor
